# Fritzing sketch FallDetection (saved by Fritzing 0.9.4)

parts:
  part = Raspberry Pi 4B
  part_2 = InvenSense MPU6050

nets:
  3V3: part.3V3, part_2.VCC
  N1: part.GPIO2, part_2.SDA
  N2: part.GPIO3, part.GPIO4, part_2.SCL
  GND: part.GND, part.GPIO17, part_2.GND
