# Fritzing sketch Environment_IoT (saved by Fritzing 0.9.4)
breadboards: 1

parts:
  Mod1 = Raspberry Pi 4B
  R1 = Resistor [tolerance=±5% resistance=10 package=THT]
  AM1 = AM2302_Humidity_and_Temperature_Sensor

nets:
  N1: Mod1.3V3, Mod1.GPIO24, R1.Pin_0, R1.Pin_1, AM1.connector1, AM1.connector2
  N2: Mod1.GPIO3, Mod1.GND, Mod1.GPIO10, Mod1.GPIO7, Mod1.ID_SD, Mod1.ID_SC, Mod1.GPIO5, Mod1.GPIO6, Mod1.GPIO12, Mod1.GPIO13, AM1.connector3
