# Fritzing sketch IoTDoor (saved by Fritzing 0.9.4)

parts:
  U1 = ESP32-38PinWide [part_number=ESP32-38PinWide]
  MOTOR1 = 28BYJ-48 Stepper Motor
  BREAKOUT1 = ULN2003A breakout board

nets:
  N1: U1.EN, U1.GPIO36, BREAKOUT1.In_4
  N2: U1.GPIO39, BREAKOUT1.In_3
  N3: U1.GPIO34, BREAKOUT1.In_2
  N4: U1.GPIO35, BREAKOUT1.In_1
  N5: U1.GND, BREAKOUT1.0V
  VIN: U1.VIN, BREAKOUT1.+5V
  N6: MOTOR1.RED, BREAKOUT1.RED_wire
  N7: MOTOR1.ORANGE, BREAKOUT1.ORANGE_wire
  N8: MOTOR1.YELLOW, BREAKOUT1.YELLOW_wire
  N9: MOTOR1.PINK, BREAKOUT1.PINK_wire
  N10: MOTOR1.BLUE, BREAKOUT1.BLUE_wire

custom parts:
  ESP32-38PinWide: Generic 38-Pin ESP32 with wide format (only access to one side of pins on a breadboard) based on Stephen Lilley's HiLetgo ESP-WROOM-32 ESP32 ESP-32S Development Board.
  ULN2003A breakout board: ULN2003A 7-way Darlington Transistor Driver on breakoutboard
